// Logisim project proj_2.circ as structural Verilog: 8 circuits, main circuit main
module main (
  input  in_1,
  input  in_2,
  input  in_3,
  input  in_4,
  input  in_5,
  input  in_6,
  input  in_7,
  input  in_8,
  input  in_9,
  input  in_10,
  input  in_11
);

  wire idk_yet_1_out_12;
  wire [4:0] bin_led_driver_1_out_2, bin_led_driver_1_out_3, bin_led_driver_1_out_4, bin_led_driver_2_out_2,
       bin_led_driver_2_out_3, bin_led_driver_2_out_4, bin_led_driver_3_out_2, bin_led_driver_3_out_3,
       bin_led_driver_3_out_4, bin_led_driver_4_out_2, bin_led_driver_4_out_3, bin_led_driver_4_out_4,
       bin_led_driver_5_out_2, bin_led_driver_5_out_3, bin_led_driver_5_out_4, bin_led_driver_6_out_2,
       bin_led_driver_6_out_3, bin_led_driver_6_out_4, bin_led_driver_7_out_2, bin_led_driver_7_out_3,
       bin_led_driver_7_out_4, bin_led_driver_8_out_2, bin_led_driver_8_out_3, bin_led_driver_8_out_4,
       bin_led_driver_9_out_2, bin_led_driver_9_out_3, bin_led_driver_9_out_4, bin_led_driver_10_out_2,
       bin_led_driver_10_out_3, bin_led_driver_10_out_4, bin_led_driver_11_out_2, bin_led_driver_11_out_3,
       bin_led_driver_11_out_4, t_or_f_1_out_2, t_or_f_1_out_3, t_or_f_1_out_4;

  DotMatrix #(.matrixcols(3), .matrixrows(5)) dotmatrix_1 (
    .col0(bin_led_driver_2_out_2), .col1(bin_led_driver_2_out_3), .col2(bin_led_driver_2_out_4));
  DotMatrix #(.matrixcols(3), .matrixrows(5)) dotmatrix_2 (
    .col0(bin_led_driver_1_out_2), .col1(bin_led_driver_1_out_3), .col2(bin_led_driver_1_out_4));
  bin_led_driver bin_led_driver_1 (
    .out_2(bin_led_driver_1_out_2), .out_3(bin_led_driver_1_out_3), .out_4(bin_led_driver_1_out_4),
    .in_1(in_2));
  bin_led_driver bin_led_driver_2 (
    .out_2(bin_led_driver_2_out_2), .out_3(bin_led_driver_2_out_3), .out_4(bin_led_driver_2_out_4),
    .in_1(in_1));
  DotMatrix #(.matrixcols(3), .matrixrows(5)) dotmatrix_3 (
    .col0(bin_led_driver_3_out_2), .col1(bin_led_driver_3_out_3), .col2(bin_led_driver_3_out_4));
  DotMatrix #(.matrixcols(3), .matrixrows(5)) dotmatrix_4 (
    .col0(bin_led_driver_4_out_2), .col1(bin_led_driver_4_out_3), .col2(bin_led_driver_4_out_4));
  bin_led_driver bin_led_driver_3 (
    .out_2(bin_led_driver_3_out_2), .out_3(bin_led_driver_3_out_3), .out_4(bin_led_driver_3_out_4),
    .in_1(in_3));
  bin_led_driver bin_led_driver_4 (
    .out_2(bin_led_driver_4_out_2), .out_3(bin_led_driver_4_out_3), .out_4(bin_led_driver_4_out_4),
    .in_1(in_4));
  DotMatrix #(.matrixcols(3), .matrixrows(5)) dotmatrix_5 (
    .col0(bin_led_driver_5_out_2), .col1(bin_led_driver_5_out_3), .col2(bin_led_driver_5_out_4));
  DotMatrix #(.matrixcols(3), .matrixrows(5)) dotmatrix_6 (
    .col0(bin_led_driver_6_out_2), .col1(bin_led_driver_6_out_3), .col2(bin_led_driver_6_out_4));
  bin_led_driver bin_led_driver_5 (
    .out_2(bin_led_driver_5_out_2), .out_3(bin_led_driver_5_out_3), .out_4(bin_led_driver_5_out_4),
    .in_1(in_5));
  bin_led_driver bin_led_driver_6 (
    .out_2(bin_led_driver_6_out_2), .out_3(bin_led_driver_6_out_3), .out_4(bin_led_driver_6_out_4),
    .in_1(in_6));
  idk_yet idk_yet_1 (
    .out_12(idk_yet_1_out_12), .a_3(in_4), .a_2(in_3), .a_1(in_2), .a_0(in_1), .b_3(in_11), .b_2(in_10),
    .b_1(in_9), .b_0(in_8), .c_1(in_6), .c_2(in_7), .c_0(in_5));
  DotMatrix #(.matrixcols(3), .matrixrows(5)) dotmatrix_7 (
    .col0(bin_led_driver_7_out_2), .col1(bin_led_driver_7_out_3), .col2(bin_led_driver_7_out_4));
  bin_led_driver bin_led_driver_7 (
    .out_2(bin_led_driver_7_out_2), .out_3(bin_led_driver_7_out_3), .out_4(bin_led_driver_7_out_4),
    .in_1(in_7));
  DotMatrix #(.matrixcols(3), .matrixrows(5)) dotmatrix_8 (
    .col0(bin_led_driver_8_out_2), .col1(bin_led_driver_8_out_3), .col2(bin_led_driver_8_out_4));
  DotMatrix #(.matrixcols(3), .matrixrows(5)) dotmatrix_9 (
    .col0(bin_led_driver_10_out_2), .col1(bin_led_driver_10_out_3), .col2(bin_led_driver_10_out_4));
  DotMatrix #(.matrixcols(3), .matrixrows(5)) dotmatrix_10 (
    .col0(bin_led_driver_9_out_2), .col1(bin_led_driver_9_out_3), .col2(bin_led_driver_9_out_4));
  bin_led_driver bin_led_driver_8 (
    .out_2(bin_led_driver_8_out_2), .out_3(bin_led_driver_8_out_3), .out_4(bin_led_driver_8_out_4),
    .in_1(in_8));
  bin_led_driver bin_led_driver_9 (
    .out_2(bin_led_driver_9_out_2), .out_3(bin_led_driver_9_out_3), .out_4(bin_led_driver_9_out_4),
    .in_1(in_9));
  DotMatrix #(.matrixcols(3), .matrixrows(5)) dotmatrix_11 (
    .col0(bin_led_driver_11_out_2), .col1(bin_led_driver_11_out_3), .col2(bin_led_driver_11_out_4));
  bin_led_driver bin_led_driver_10 (
    .out_2(bin_led_driver_10_out_2), .out_3(bin_led_driver_10_out_3), .out_4(bin_led_driver_10_out_4),
    .in_1(in_10));
  bin_led_driver bin_led_driver_11 (
    .out_2(bin_led_driver_11_out_2), .out_3(bin_led_driver_11_out_3), .out_4(bin_led_driver_11_out_4),
    .in_1(in_11));
  DotMatrix #(.matrixcols(3), .matrixrows(5)) dotmatrix_12 (
    .col0(t_or_f_1_out_2), .col1(t_or_f_1_out_3), .col2(t_or_f_1_out_4));
  t_or_f t_or_f_1 (.out_2(t_or_f_1_out_2), .out_3(t_or_f_1_out_3), .out_4(t_or_f_1_out_4), .in_1(idk_yet_1_out_12));

  // Notes on the sheet:
  //   000:<  001:<=  010:==  011:>=  100:>
endmodule

module bin_led_driver (
  input  in_1,
  output [4:0] out_2,
  output [4:0] out_3,
  output [4:0] out_4
);

  not not_1 (out_2[3], in_1);
  DotMatrix #(.matrixcols(3), .matrixrows(5)) dotmatrix_1 (
    .col0({1'b1, {3{out_2[3]}}, 1'b1}), .col1({1'b1, {3{in_1}}, 1'b1}), .col2({{4{out_4[4]}}, 1'b1}));
  not not_2 (out_4[4], in_1);

  assign {out_2[4], out_2[2:0]} = {1'b1, {2{out_2[3]}}, 1'b1};
  assign out_3 = {1'b1, {3{in_1}}, 1'b1};
  assign out_4[3:0] = {{3{out_4[4]}}, 1'b1};
endmodule

module _2_bit_adder (
  input  a_1,
  input  a_0,
  input  b_1,
  input  b_0,
  input  c_i,
  output s_1,
  output s_0,
  output c_0
);

  wire n1_bit_adder_2_c_out;

  _1_bit_adder u_1_bit_adder_1 (.a(a_1), .b(b_1), .c_in(n1_bit_adder_2_c_out), .s(s_0), .c_out(c_0));
  _1_bit_adder u_1_bit_adder_2 (.a(a_0), .b(b_0), .c_in(c_i), .s(s_1), .c_out(n1_bit_adder_2_c_out));
endmodule

module _1_bit_adder (
  input  a,
  input  b,
  input  c_in,
  output s,
  output c_out
);

  wire nand_1_out, nand_2_out, nand_3_out, nand_4_out, nand_5_out, nand_6_out, nand_7_out;

  nand nand_1 (nand_1_out, a, b);
  nand nand_2 (nand_2_out, a, nand_1_out);
  nand nand_3 (nand_3_out, nand_1_out, b);
  nand nand_4 (nand_4_out, nand_2_out, nand_3_out);
  nand nand_5 (nand_5_out, nand_4_out, c_in);
  nand nand_6 (nand_6_out, nand_4_out, nand_5_out);
  nand nand_7 (nand_7_out, nand_5_out, c_in);
  nand nand_8 (c_out, nand_5_out, nand_1_out);
  nand nand_9 (s, nand_6_out, nand_7_out);
endmodule

module _1_bit_comparator (
  input  eq_i,
  input  lt_i,
  input  gt_i,
  input  a,
  input  b,
  output lt_o,
  output eq_o,
  output gt_o
);

  wire and_1_out, and_2_out, and_3_out, and_4_out, nor_1_out, not_1_out, not_2_out;

  not not_1 (not_1_out, a);
  not not_2 (not_2_out, b);
  and and_1 (and_1_out, not_1_out, b);
  and and_2 (and_2_out, a, not_2_out);
  nor nor_1 (nor_1_out, and_1_out, and_2_out);
  and and_3 (and_3_out, lt_i, nor_1_out);
  and and_4 (and_4_out, gt_i, nor_1_out);
  or or_1 (lt_o, and_1_out, and_3_out);
  and and_5 (eq_o, eq_i, nor_1_out);
  or or_2 (gt_o, and_4_out, and_2_out);
endmodule

module _4_bit_comparator (
  input  a_3,
  input  b_3,
  input  a_2,
  input  b_2,
  input  a_1,
  input  b_1,
  input  a_0,
  input  b_0,
  input  eq_i,
  input  lt_i,
  input  gt_i,
  output eq_o,
  output lt_o,
  output gt_o
);

  wire n1_bit_comparator_1_eq_o, n1_bit_comparator_1_gt_o, n1_bit_comparator_1_lt_o,
       n1_bit_comparator_3_eq_o, n1_bit_comparator_3_gt_o, n1_bit_comparator_3_lt_o,
       n1_bit_comparator_4_eq_o, n1_bit_comparator_4_gt_o, n1_bit_comparator_4_lt_o;

  _1_bit_comparator u_1_bit_comparator_1 (
    .eq_i(n1_bit_comparator_3_eq_o), .lt_i(n1_bit_comparator_3_lt_o), .gt_i(n1_bit_comparator_3_gt_o),
    .a(a_2), .b(b_2), .lt_o(n1_bit_comparator_1_lt_o), .eq_o(n1_bit_comparator_1_eq_o),
    .gt_o(n1_bit_comparator_1_gt_o));
  _1_bit_comparator u_1_bit_comparator_2 (
    .eq_i(n1_bit_comparator_1_eq_o), .lt_i(n1_bit_comparator_1_lt_o), .gt_i(n1_bit_comparator_1_gt_o),
    .a(a_3), .b(b_3), .lt_o(lt_o), .eq_o(eq_o), .gt_o(gt_o));
  _1_bit_comparator u_1_bit_comparator_3 (
    .eq_i(n1_bit_comparator_4_eq_o), .lt_i(n1_bit_comparator_4_lt_o), .gt_i(n1_bit_comparator_4_gt_o),
    .a(a_1), .b(b_1), .lt_o(n1_bit_comparator_3_lt_o), .eq_o(n1_bit_comparator_3_eq_o),
    .gt_o(n1_bit_comparator_3_gt_o));
  _1_bit_comparator u_1_bit_comparator_4 (
    .eq_i(eq_i), .lt_i(lt_i), .gt_i(gt_i), .a(a_0), .b(b_0), .lt_o(n1_bit_comparator_4_lt_o),
    .eq_o(n1_bit_comparator_4_eq_o), .gt_o(n1_bit_comparator_4_gt_o));
endmodule

module idk_yet (
  input  a_3,
  input  a_2,
  input  a_1,
  input  a_0,
  input  b_3,
  input  b_2,
  input  b_1,
  input  b_0,
  input  c_0,
  input  c_1,
  input  c_2,
  output out_12
);

  wire n4_bit_comparator_1_eq_o, n4_bit_comparator_1_gt_o, n4_bit_comparator_1_lt_o, or_1_out, or_2_out;

  Multiplexer #(.select(3), .enable("false")) multiplexer_1 (
    .in0(n4_bit_comparator_1_lt_o), .in1(or_2_out), .in2(n4_bit_comparator_1_eq_o), .in3(or_1_out),
    .in4(n4_bit_comparator_1_gt_o), .out(out_12), .sel({c_0, c_1, c_2}));  // open: in5, in6, in7
  or or_1 (or_1_out, n4_bit_comparator_1_gt_o, n4_bit_comparator_1_eq_o);
  or or_2 (or_2_out, n4_bit_comparator_1_eq_o, n4_bit_comparator_1_lt_o);
  _4_bit_comparator u_4_bit_comparator_1 (
    .eq_o(n4_bit_comparator_1_eq_o), .lt_o(n4_bit_comparator_1_lt_o), .gt_o(n4_bit_comparator_1_gt_o),
    .eq_i(1'b1), .lt_i(1'b0), .gt_i(1'b0), .a_3(a_3), .b_3(b_3), .a_2(a_2), .b_2(b_2), .a_1(a_1), .b_1(b_1),
    .a_0(a_0), .b_0(b_0));
endmodule

module t_or_f (
  input  in_1,
  output [4:0] out_2,
  output [4:0] out_3,
  output [4:0] out_4
);

  not not_1 (out_2[3], in_1);
  DotMatrix #(.matrixcols(3), .matrixrows(5)) dotmatrix_1 (
    .col0({1'b1, {4{out_2[3]}}}), .col1({1'b1, in_1, 1'b1, {2{in_1}}}), .col2({2'b10, out_4[2], 2'b00}));
  not not_2 (out_4[2], in_1);

  assign {out_2[4], out_2[2:0]} = {1'b1, {3{out_2[3]}}};
  assign out_3 = {1'b1, in_1, 1'b1, {2{in_1}}};
  assign {out_4[4:3], out_4[1:0]} = 4'b1000;
endmodule
